# Fritzing sketch FormulaIno (saved by Fritzing 0.9.4)

parts:
  Componente1 = Arduino Uno (Rev3) - ICSP
  Componente2 = Arduino USB Host Shield
  M1 = DC Motor  # not connected
  L298N1 = L298N DC motor driver
  M2 = DC Motor  # not connected
  J1 = Basic Servo

nets:
  5V: Componente1.5V, J1.vcc
  N1: Componente2.5V-ARDUINO, L298N1.5V#7
  N2: Componente2.D2, L298N1.IN1
  N3: Componente2.D3, L298N1.ENA
  N4: Componente2.D4, L298N1.IN2
  N5: Componente2.D5, L298N1.5V#10, L298N1.ENB
  N6: Componente2.D6, L298N1.IN3
  N7: Componente2.RESET, L298N1.IN4
  N8: Componente2.INT, J1.pulse
  GND: Componente2.GND, L298N1.GND, J1.gnd

custom parts:
  L298N DC motor driver: 2x DC motor driver with 78M05 positive voltage regulator (7..35 V) L298N: max 46 V, 2 A Set 5 V Enable jumper to enable 5 V regultor (needed for the L298N) and +5 V output at screw terminal or supply external +5 V at screw terminal Set ENA and/or ENB to +5 V to enable motor permanently or supply ENA and/or ENB with PWM signal IN1 and IN2 set rotation directory for motor A (OUT1/OUT2) IN2 and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
